# Fritzing sketch Black Maze Box v2 (saved by Fritzing 0.9.1b)
stripboards: 3

parts:
  Part1 = Arduino Uno (Rev3)
  Part3 = Electric Imp Breakout
  Part4 = Arduino Prototyping Shield
  Part6 = Logic Level Converter

nets:
  N1: Part1.D8, Part4.D8
  GND: Part1.GND, Part3.11, Part4.GND, Part6.GND
  3V3: Part1.3V3, Part3.10, Part4.3.3V, Part6.LV
  5V: Part1.5V, Part4.+5V, Part6.HV
  N2: Part3.3, Part6.RX_LV
  N3: Part3.4, Part6.TX_LV
  N4: Part3.12, Part3.13

custom parts:
  Electric Imp Breakout: Electric Imp Breakout Board with onboard 3.3V regulated power supply
